// Logisim project s-mips.circ as structural Verilog
module S_MIPS_Board (
  input  DESHABILITAR_DISPATCHER,
  output halt
);

  wire button_1_out, CLK, CS, d_ff_1_q, LCLR, LoadRAM, LoadRAMOn, LW, R_R_W, R_W, ram_dispatcher_1_finished,
       RCS, Reset_out, RST, TTY_EN;
  wire [2:0] KDB;
  wire [3:0] LMask, Mask, ram_1_read_time, ram_1_write_time, RMask;
  wire [6:0] KDB_DATA, TTY_DATA;
  wire [15:0] Addr, LAddr, RAddr;
  wire [31:0] I0, I1, I2, I3, LData, ram_1_data_out_0, ram_1_data_out_1, ram_1_data_out_2, ram_1_data_out_3,
       RI0, RI1, RI2, RI3;

  TTY #(.rows(25), .cols(80)) tty_1 (.data(TTY_DATA), .clk(CLK), .we(TTY_EN), .clr(RST));
  not not_1 (LoadRAMOn, ram_dispatcher_1_finished);
  RAM_Dispatcher ram_dispatcher_1 (
    .WriteTime(ram_1_write_time), .Clock(CLK), .Data(LData), .Address(LAddr), .Mask(LMask),
    .Finished(ram_dispatcher_1_finished), .Write(LW), .CLR(LCLR));
  Keyboard #(.buflen(64)) keyboard_1 (.clk(CLK), .re(KDB[0]), .avail(KDB[2]), .data(KDB_DATA));  // open: clr
  RAM ram_1 (
    .Address(RAddr), .Data_Out_0(ram_1_data_out_0), .Data_Out_1(ram_1_data_out_1),
    .Data_Out_2(ram_1_data_out_2), .Data_Out_3(ram_1_data_out_3), .Data_In_0(RI0), .Data_In_1(RI1),
    .Data_In_2(RI2), .Data_In_3(RI3), .Mask(RMask), .nRead_Write(R_R_W), .Chip_Select(RCS),
    .Read_Time(ram_1_read_time), .Reset(button_1_out), .Write_Time(ram_1_write_time));
  Button button_1 (.out(button_1_out));
  D_Flip_Flop d_ff_1 (.clk(CLK), .D(1'b1), .Q(d_ff_1_q), .reset(Reset_out));  // open: Qn, preset, en
  Button Reset (.out(Reset_out));
  S_MIPS s_mips_1 (
    .Kbd_Enable(KDB[0]), .Address(Addr), .Kbd_Clear(KDB[1]), .Kbd_Available(KDB[2]), .RAM_In_0(I0),
    .Kbd_ASCII_Data(KDB_DATA), .RAM_In_1(I1), .TTY_Enable(TTY_EN), .RAM_In_2(I2), .RAM_In_3(I3),
    .TTY_ASCII_Data(TTY_DATA), .Reset(RST), .RAM_Out_0(ram_1_data_out_0), .Clock(CLK),
    .RAM_Out_1(ram_1_data_out_1), .Stop(halt), .RAM_Out_2(ram_1_data_out_2), .RAM_Out_3(ram_1_data_out_3),
    .Mask(Mask), .Read_Time(ram_1_read_time), .Write_Time(ram_1_write_time), .nRead_Write(R_W),
    .Chip_Select(CS));
  D_Flip_Flop d_ff_2 (.clk(CLK), .D(d_ff_1_q), .Qn(LCLR), .reset(Reset_out));  // open: Q, preset, en
  or or_1 (RST, LCLR, LoadRAM);
  Clock clock_1 (.out(CLK));
  Multiplexer #(.width(32), .enable("false")) multiplexer_1 (.in0(I0), .in1(LData), .out(RI0), .sel(LoadRAM));
  Multiplexer #(.width(32), .enable("false")) multiplexer_2 (.in0(I1), .in1(LData), .out(RI1), .sel(LoadRAM));
  Multiplexer #(.width(32), .enable("false")) multiplexer_3 (.in0(I2), .in1(LData), .out(RI2), .sel(LoadRAM));
  Multiplexer #(.width(32), .enable("false")) multiplexer_4 (.in0(I3), .in1(LData), .out(RI3), .sel(LoadRAM));
  and and_1 (LoadRAM, ~DESHABILITAR_DISPATCHER, LoadRAMOn);  // AND_Gate
  Multiplexer #(.width(16), .enable("false")) multiplexer_5 (.in0(Addr), .in1(LAddr), .out(RAddr), .sel(LoadRAM));
  Multiplexer #(.width(4), .enable("false")) multiplexer_6 (.in0(Mask), .in1(LMask), .out(RMask), .sel(LoadRAM));
  Multiplexer #(.enable("false")) multiplexer_7 (.in0(CS), .in1(LW), .out(RCS), .sel(LoadRAM));
  Multiplexer #(.enable("false")) multiplexer_8 (.in0(R_W), .in1(LW), .out(R_R_W), .sel(LoadRAM));

  // Notes on the sheet:
  //   NO MODIFICAR
  //   Keyboard
endmodule

module RAM (
  input  [15:0] Address,
  input  [31:0] Data_In_0,
  input  [31:0] Data_In_1,
  input  [31:0] Data_In_2,
  input  [31:0] Data_In_3,
  input  [3:0] Mask,
  input  nRead_Write,
  input  Chip_Select,
  input  Reset,
  output [31:0] Data_Out_0,
  output [31:0] Data_Out_1,
  output [31:0] Data_Out_2,
  output [31:0] Data_Out_3,
  output [3:0] Read_Time,
  output [3:0] Write_Time
);

  wire and_2_out, and_3_out, and_4_out, and_5_out, and_6_out, and_7_out, and_8_out, and_9_out, Changed, CLK,
       comparator_2_eq, comparator_3_eq, comparator_4_eq, comparator_5_eq, comparator_6_eq, Count,
       demultiplexer_3_out0, Idle, Idle_q, Load, Load0, Load1, nand_1_out, or_1_out, or_2_out, or_3_out,
       or_4_out, or_5_out, or_6_out, or_7_out, or_8_out, or_9_out, or_10_out, Proc_q, Update_Mem, Zero_Time;
  wire [3:0] counter_1_q, multiplexer_1_out, subtractor_1_out;
  wire [31:0] register_1_q, register_2_q, register_3_q, register_4_q, register_5_q;

  // Probe on 4'b0011
  // Probe on 4'b0010
  Multiplexer #(.width(4), .enable("false")) multiplexer_1 (
    .in0(4'b0011), .in1(4'b0010), .out(multiplexer_1_out), .sel(nRead_Write));
  or or_1 (or_1_out, Idle, Update_Mem);
  or or_2 (or_2_out, ~Chip_Select, Reset);  // OR_Gate
  Subtractor #(.width(4)) subtractor_1 (.a(multiplexer_1_out), .b(4'b0010), .out(subtractor_1_out));  // open: bin, bout
  D_Flip_Flop u_Idle (.clk(CLK), .D(or_1_out), .Q(Idle_q), .preset(or_2_out));  // open: Qn, en, reset
  Demultiplexer #(.enable("false")) demultiplexer_1 (.out0(Idle), .out1(Load0), .in(Idle_q), .sel(Changed));
  // Probe on counter_1_q
  Counter #(.width(4), .max('hf)) counter_1 (
    .load(Load), .D(subtractor_1_out), .count(Count), .Q(counter_1_q), .clk(CLK), .clr(or_3_out));  // open: carry
  or or_3 (or_3_out, ~Chip_Select, Reset);  // OR_Gate
  Comparator #(.width(4), .mode("unsigned")) comparator_1 (
    .a(4'b0000), .b(counter_1_q), .eq(Zero_Time));  // open: gt, lt
  or or_4 (or_4_out, Count, Load0, Load1);
  Register #(.width(32)) register_1 (.D(Data_In_0), .en(Chip_Select), .Q(register_1_q), .clk(CLK), .clr(or_5_out));
  or or_5 (or_5_out, ~Chip_Select, Reset);  // OR_Gate
  Register #(.width(32)) register_2 (.D(Data_In_1), .en(Chip_Select), .Q(register_2_q), .clk(CLK), .clr(or_6_out));
  or or_6 (or_6_out, ~Chip_Select, Reset);  // OR_Gate
  Register #(.width(32)) register_3 (.D(Data_In_2), .en(Chip_Select), .Q(register_3_q), .clk(CLK), .clr(or_7_out));
  or or_7 (or_7_out, ~Chip_Select, Reset);  // OR_Gate
  Register #(.width(32)) register_4 (.D(Data_In_3), .en(Chip_Select), .Q(register_4_q), .clk(CLK), .clr(or_8_out));
  or or_8 (or_8_out, ~Chip_Select, Reset);  // OR_Gate
  Register #(.width(32)) register_5 (
    .D({{11{1'b1}}, nRead_Write, Mask, Address}), .en(Chip_Select), .Q(register_5_q), .clk(CLK),
    .clr(or_9_out));
  or or_9 (or_9_out, ~Chip_Select, Reset);  // OR_Gate
  D_Flip_Flop Proc (.clk(CLK), .D(or_4_out), .Q(Proc_q), .reset(or_10_out));  // open: Qn, preset, en
  or or_10 (or_10_out, ~Chip_Select, Reset);  // OR_Gate
  Demultiplexer #(.enable("false")) demultiplexer_2 (
    .out0(Count), .out1(Update_Mem), .in(demultiplexer_3_out0), .sel(Zero_Time));
  Demultiplexer #(.enable("false")) demultiplexer_3 (
    .out0(demultiplexer_3_out0), .out1(Load1), .in(Proc_q), .sel(Changed));
  Clock clock_1 (.out(CLK));
  Comparator #(.width(32)) comparator_2 (.a(register_1_q), .b(Data_In_0), .eq(comparator_2_eq));  // open: gt, lt
  Comparator #(.width(32)) comparator_3 (.a(register_2_q), .b(Data_In_1), .eq(comparator_3_eq));  // open: gt, lt
  Comparator #(.width(32)) comparator_4 (.a(register_3_q), .b(Data_In_2), .eq(comparator_4_eq));  // open: gt, lt
  Comparator #(.width(32)) comparator_5 (.a(register_4_q), .b(Data_In_3), .eq(comparator_5_eq));  // open: gt, lt
  Comparator #(.width(32)) comparator_6 (
    .a(register_5_q), .b({{11{1'b1}}, nRead_Write, Mask, Address}), .eq(comparator_6_eq));  // open: gt, lt
  nand nand_1 (nand_1_out, comparator_6_eq, comparator_2_eq, comparator_3_eq, comparator_4_eq, comparator_5_eq);
  and and_1 (Changed, nand_1_out, Chip_Select);
  or or_11 (Load, Count, Load1, Load0);
  and and_2 (and_2_out, Mask[0], Update_Mem, nRead_Write);
  and and_3 (and_3_out, Mask[1], Update_Mem, nRead_Write);
  and and_4 (and_4_out, Mask[2], Update_Mem, nRead_Write);
  and and_5 (and_5_out, Mask[3], Update_Mem, nRead_Write);
  RAM_part #(.addrWidth(16), .dataWidth(32), .bus("separate")) ram_1 (
    .addr(Address), .din(Data_In_0), .data(Data_Out_0), .str(and_2_out), .sel(Chip_Select), .clk(CLK),
    .ld(and_6_out), .clr(Reset));
  and and_6 (and_6_out, ~nRead_Write, Idle);  // AND_Gate
  RAM_part #(.addrWidth(16), .dataWidth(32), .bus("separate")) ram_2 (
    .addr(Address), .din(Data_In_1), .data(Data_Out_1), .str(and_3_out), .sel(Chip_Select), .clk(CLK),
    .ld(and_7_out), .clr(Reset));
  and and_7 (and_7_out, ~nRead_Write, Idle);  // AND_Gate
  RAM_part #(.addrWidth(16), .dataWidth(32), .bus("separate")) ram_3 (
    .addr(Address), .din(Data_In_2), .data(Data_Out_2), .str(and_4_out), .sel(Chip_Select), .clk(CLK),
    .ld(and_8_out), .clr(Reset));
  and and_8 (and_8_out, ~nRead_Write, Idle);  // AND_Gate
  RAM_part #(.addrWidth(16), .dataWidth(32), .bus("separate")) ram_4 (
    .addr(Address), .din(Data_In_3), .data(Data_Out_3), .str(and_5_out), .sel(Chip_Select), .clk(CLK),
    .ld(and_9_out), .clr(Reset));
  and and_9 (and_9_out, ~nRead_Write, Idle);  // AND_Gate

  assign Read_Time = 4'b0011;
  assign Write_Time = 4'b0010;

  // Other names for the same wires on the sheet: M0 = Mask[0]; M1 = Mask[1]; M2 = Mask[2]; M3 = Mask[3];
  //   RW = nRead_Write; CLR = Reset; CS = Chip_Select; Load2 = Count

  // Notes on the sheet:
  //   NO MODIFICAR
  //   excepto quizás los valores RT y WT
  //   BANK0
  //   BANK1
  //   BANK2
  //   BANK3
endmodule

module S_MIPS (
  input  Kbd_Available,
  input  [6:0] Kbd_ASCII_Data,
  input  [31:0] RAM_Out_0,
  input  [31:0] RAM_Out_1,
  input  Reset,
  input  [31:0] RAM_Out_2,
  input  Clock,
  input  [31:0] RAM_Out_3,
  input  [3:0] Read_Time,
  input  [3:0] Write_Time,
  output Kbd_Enable,
  output [15:0] Address,
  output Kbd_Clear,
  output TTY_Enable,
  output [6:0] TTY_ASCII_Data,
  output Stop,
  output [31:0] RAM_In_0,
  output [31:0] RAM_In_1,
  output [31:0] RAM_In_2,
  output [31:0] RAM_In_3,
  output [3:0] Mask,
  output nRead_Write,
  output Chip_Select
);


  // Other names for the same wires on the sheet: CLK = Clock; CLR = Reset; CS = Chip_Select;
  //   KBD_AVAIL = Kbd_Available; KBD_CLR = Kbd_Clear; KBD_DATA[6:0] = Kbd_ASCII_Data; RAM_A[15:0] = Address;
  //   RAM_INPUT_0[31:0] = RAM_In_0; RAM_INPUT_1[31:0] = RAM_In_1; RAM_INPUT_2[31:0] = RAM_In_2;
  //   RAM_INPUT_3[31:0] = RAM_In_3; RAM_MASK[3:0] = Mask; RAM_OUTPUT_0[31:0] = RAM_Out_0;
  //   RAM_OUTPUT_1[31:0] = RAM_Out_1; RAM_OUTPUT_2[31:0] = RAM_Out_2; RAM_OUTPUT_3[31:0] = RAM_Out_3;
  //   RW = nRead_Write; TTY_DATA[6:0] = TTY_ASCII_Data

  // Notes on the sheet:
  //   RAM ADDRESS
  //   DATA FROM RAM
  //   DATA TO RAM
  //   DATA WRITE MASK
  //   RAM TIMING
  //   RAM CONTROL
  //   KEYBOARD
  //   TTY
  //   SEQUENCING
endmodule

module RAM_Dispatcher (
  input  [3:0] WriteTime,
  input  Clock,
  input  CLR,
  output [31:0] Data,
  output [15:0] Address,
  output [3:0] Mask,
  output Finished,
  output Write
);

  wire demultiplexer_2_out1, demultiplexer_3_out1, End, IDLE_q, IncAddr, Load, or_1_out, or_2_out, While_q,
       WriteEnd;
  wire [3:0] counter_1_q;
  wire [31:0] CurrentAddress_q;

  Counter #(.width(32), .max('hffffffff)) CurrentAddress (
    .count(IncAddr), .Q({CurrentAddress_q[31:18], Address, CurrentAddress_q[1:0]}), .clk(Clock), .clr(CLR));  // open: load, D, carry
  or or_1 (or_1_out, IncAddr, demultiplexer_3_out1, Finished);
  D_Flip_Flop IDLE (.clk(Clock), .D(or_1_out), .Q(IDLE_q), .preset(CLR));  // open: Qn, en, reset
  Demultiplexer #(.enable("false")) demultiplexer_1 (.out0(Load), .out1(Finished), .in(IDLE_q), .sel(End));
  D_Flip_Flop While (.clk(Clock), .D(or_2_out), .Q(While_q), .reset(CLR));  // open: Qn, preset, en
  or or_2 (or_2_out, Write, Load);
  RAM_part #(.addrWidth(18), .dataWidth(32)) ram_1 (
    .addr({Address, CurrentAddress_q[1:0]}), .data(Data), .clk(Clock));  // open: sel, ld, clr
  Demultiplexer #(.enable("false")) demultiplexer_2 (
    .out0(Write), .out1(demultiplexer_2_out1), .in(While_q), .sel(WriteEnd));
  Decoder #(.select(2)) decoder_1 (
    .out0(Mask[0]), .out1(Mask[1]), .out2(Mask[2]), .out3(Mask[3]), .sel(CurrentAddress_q[1:0]));  // open: en
  Demultiplexer #(.enable("false")) demultiplexer_3 (
    .out0(IncAddr), .out1(demultiplexer_3_out1), .in(demultiplexer_2_out1), .sel(End));
  Counter #(.width(4), .max('hf)) counter_1 (
    .load(Load), .D(WriteTime), .count(Write), .Q(counter_1_q), .clk(Clock));  // open: carry, clr
  Comparator #(.width(32)) comparator_1 (.a(Data), .b({32{1'b1}}), .eq(End));  // open: gt, lt
  Comparator #(.width(4)) comparator_2 (.a(4'b0000), .b(counter_1_q), .eq(WriteEnd));  // open: gt, lt

  // Other names for the same wires on the sheet: CLK = Clock; Count = Write; WT[3:0] = WriteTime
endmodule

module Data_Path_2 (
  input  Clk,
  input  Reset,
  input  Write_PC,
  input  Write_Inst_Memory,
  input  Write_RF,
  input  Write_SP,
  input  Write_HL,
  input  [31:0] RAM,
  input  [25:0] Target,
  input  [2:0] ALU_Op,
  input  [31:0] Constant,
  input  [2:0] Flag_Selector,
  input  [1:0] Branch_Selector,
  input  [4:0] A_Selector,
  input  [4:0] B_Selector,
  input  [6:0] KBD_Data,
  input  KBD_Available,
  input  [4:0] Data_Address,
  input  [2:0] Data_In_Selector,
  input  [1:0] Address_Selector,
  input  [1:0] ALU_B_In,
  output [31:0] RAM_Address,
  output [31:0] RAM_Out,
  output [6:0] tty_out
);

  wire N, Z;
  wire [31:0] bit_extender_1_out, Hi, Hi_In, IM, Kbd, Lo, Lo_In, multiplexer_1_out, multiplexer_3_out, PC,
       PC_prime, R, Rnd, SP;
  wire [31:7] RS;

  Register #(.width(32)) Instruction_Memory (.D(RAM), .en(Write_Inst_Memory), .Q(IM), .clk(Clk), .clr(Reset));
  Multiplexer #(.select(3), .width(32)) multiplexer_1 (
    .in0(RAM), .in1(Hi), .in2(Lo), .in3(R), .in4(Rnd), .in5(Kbd), .out(multiplexer_1_out),
    .sel(Data_In_Selector));  // open: in6, in7, en
  Random #(.width(32)) u_RND (.clk(Clk), .out(Rnd), .clr(Reset));  // open: next
  assign bit_extender_1_out = {{25{1'b0}}, KBD_Data};  // Bit_Extender bit_extender_1
  Register_File register_file_1 (
    .In(multiplexer_1_out), .Sa(A_Selector), .Sb(B_Selector), .W_R(Write_RF), .DA(Data_Address), .Hi(Hi_In),
    .Lo(Lo_In), .Clk(Clk), .Rst(Reset), .HL_R_W(Write_HL), .SP_R_W(Write_SP), .A_out({RS, tty_out}),
    .B_out(RAM_Out), .Hi_2(Hi), .Lo_2(Lo), .SP_Output(SP));
  Multiplexer #(.width(32)) multiplexer_2 (
    .in0({32{1'b1}}), .in1(bit_extender_1_out), .out(Kbd), .sel(KBD_Available));  // open: en
  Branch_Control branch_control_1 (
    .PC(PC), .Target(Target), .Constant(Constant), .Register_Value({RS, tty_out}),
    .Branch_Type_Selector(Branch_Selector), .Flag_Selector(Flag_Selector), .Zero_Flag(Z), .Negative_Flag(N),
    .PC_prime(PC_prime));
  Register #(.width(32)) u_PC (.D(PC_prime), .en(Write_PC), .Q(PC), .clk(Clk), .clr(Reset));
  Multiplexer #(.select(2), .width(32)) multiplexer_3 (
    .in0(RAM_Out), .in1(32'h4), .in2(Constant), .out(multiplexer_3_out), .sel(ALU_B_In));  // open: in3, en
  ALU alu_1 (
    .A({RS, tty_out}), .B(multiplexer_3_out), .Op(ALU_Op), .Result(R), .Lo(Lo_In), .Hi(Hi_In), .Zero(Z),
    .Negative(N));
  Multiplexer #(.select(2), .width(32)) multiplexer_4 (
    .in0(IM), .in1(SP), .in2(PC), .out(RAM_Address), .sel(Address_Selector));  // open: in3, en

  // Other names for the same wires on the sheet: AdS[1:0] = Address_Selector; AS[4:0] = A_Selector;
  //   BI[1:0] = ALU_B_In; BS[4:0] = B_Selector; BTS[1:0] = Branch_Selector; C[31:0] = Constant;
  //   DA[4:0] = Data_Address; DIS[2:0] = Data_In_Selector; FS[2:0] = Flag_Selector; RS[6:0] = tty_out; Rst = Reset;
  //   RT[31:0] = RAM_Out; W_HL = Write_HL; W_Inst = Write_Inst_Memory; W_PC = Write_PC; W_RF = Write_RF;
  //   W_SP = Write_SP
endmodule

module Register_File (
  input  [31:0] In,
  input  [4:0] Sa,
  input  [4:0] Sb,
  input  W_R,
  input  [4:0] DA,
  input  [31:0] Hi,
  input  [31:0] Lo,
  input  Clk,
  input  Rst,
  input  HL_R_W,
  input  SP_R_W,
  output [31:0] A_out,
  output [31:0] B_out,
  output [31:0] Hi_2,
  output [31:0] Lo_2,
  output [31:0] SP_Output
);

  wire SP_EN, W_R1, W_R2, W_R3, W_R4, W_R5, W_R6, W_R7, W_R8, W_R9, W_R10, W_R11, W_R12, W_R13, W_R14, W_R15,
       W_R16, W_R17, W_R18, W_R19, W_R20, W_R21, W_R22, W_R23, W_R24, W_R25, W_R26, W_R27, W_R28, W_R29,
       W_R30, W_R31;
  wire [31:0] R1, R2, R3, R4, R5, R6, R7, R8, R9, R10, R11, R12, R13, R14, R15, R16, R17, R18, R19, R20, R21,
       R22, R23, R24, R25, R26, R27, R28, R29, R30, SPOut;

  Demultiplexer #(.select(5), .enable("false")) demultiplexer_1 (
    .out1(W_R1), .out2(W_R2), .out3(W_R3), .out4(W_R4), .out5(W_R5), .out6(W_R6), .out7(W_R7), .out8(W_R8),
    .out9(W_R9), .out10(W_R10), .out11(W_R11), .out12(W_R12), .out13(W_R13), .out14(W_R14), .out15(W_R15),
    .out16(W_R16), .out17(W_R17), .out18(W_R18), .out19(W_R19), .out20(W_R20), .out21(W_R21), .out22(W_R22),
    .out23(W_R23), .out24(W_R24), .out25(W_R25), .out26(W_R26), .out27(W_R27), .out28(W_R28), .out29(W_R29),
    .out30(W_R30), .out31(W_R31), .in(W_R), .sel(DA));  // open: out0
  or or_1 (SP_EN, W_R31, SP_R_W);
  Register #(.width(32)) register_1 (.D(Hi), .en(HL_R_W), .Q(Hi_2), .clk(Clk), .clr(Rst));
  Register #(.width(32)) register_2 (.D(Lo), .en(HL_R_W), .Q(Lo_2), .clk(Clk), .clr(Rst));
  Register #(.width(32)) register_3 (.D(In), .en(W_R1), .Q(R1), .clk(Clk), .clr(Rst));
  Register #(.width(32)) register_4 (.D(In), .en(W_R2), .Q(R2), .clk(Clk), .clr(Rst));
  Register #(.width(32)) register_5 (.D(In), .en(W_R3), .Q(R3), .clk(Clk), .clr(Rst));
  Register #(.width(32)) register_6 (.D(In), .en(W_R4), .Q(R4), .clk(Clk), .clr(Rst));
  Register #(.width(32)) register_7 (.D(In), .en(W_R5), .Q(R5), .clk(Clk), .clr(Rst));
  Register #(.width(32)) register_8 (.D(In), .en(W_R6), .Q(R6), .clk(Clk), .clr(Rst));
  Register #(.width(32)) register_9 (.D(In), .en(W_R7), .Q(R7), .clk(Clk), .clr(Rst));
  Register #(.width(32)) register_10 (.D(In), .en(W_R8), .Q(R8), .clk(Clk), .clr(Rst));
  Register #(.width(32)) register_11 (.D(In), .en(W_R9), .Q(R9), .clk(Clk), .clr(Rst));
  Register #(.width(32)) register_12 (.D(In), .en(W_R10), .Q(R10), .clk(Clk), .clr(Rst));
  Register #(.width(32)) register_13 (.D(In), .en(W_R11), .Q(R11), .clk(Clk), .clr(Rst));
  Register #(.width(32)) register_14 (.D(In), .en(W_R12), .Q(R12), .clk(Clk), .clr(Rst));
  Register #(.width(32)) register_15 (.D(In), .en(W_R13), .Q(R13), .clk(Clk), .clr(Rst));
  Register #(.width(32)) register_16 (.D(In), .en(W_R14), .Q(R14), .clk(Clk), .clr(Rst));
  Register #(.width(32)) register_17 (.D(In), .en(W_R15), .Q(R15), .clk(Clk), .clr(Rst));
  Register #(.width(32)) register_18 (.D(In), .en(W_R16), .Q(R16), .clk(Clk), .clr(Rst));
  Register #(.width(32)) register_19 (.D(In), .en(W_R17), .Q(R17), .clk(Clk), .clr(Rst));
  Register #(.width(32)) register_20 (.D(In), .en(W_R18), .Q(R18), .clk(Clk), .clr(Rst));
  Register #(.width(32)) register_21 (.D(In), .en(W_R19), .Q(R19), .clk(Clk), .clr(Rst));
  Register #(.width(32)) register_22 (.D(In), .en(W_R20), .Q(R20), .clk(Clk), .clr(Rst));
  Register #(.width(32)) register_23 (.D(In), .en(W_R21), .Q(R21), .clk(Clk), .clr(Rst));
  Register #(.width(32)) register_24 (.D(In), .en(W_R22), .Q(R22), .clk(Clk), .clr(Rst));
  Register #(.width(32)) register_25 (.D(In), .en(W_R23), .Q(R23), .clk(Clk), .clr(Rst));
  Register #(.width(32)) register_26 (.D(In), .en(W_R24), .Q(R24), .clk(Clk), .clr(Rst));
  Register #(.width(32)) register_27 (.D(In), .en(W_R25), .Q(R25), .clk(Clk), .clr(Rst));
  Register #(.width(32)) register_28 (.D(In), .en(W_R26), .Q(R26), .clk(Clk), .clr(Rst));
  Register #(.width(32)) register_29 (.D(In), .en(W_R27), .Q(R27), .clk(Clk), .clr(Rst));
  Register #(.width(32)) register_30 (.D(In), .en(W_R28), .Q(R28), .clk(Clk), .clr(Rst));
  Register #(.width(32)) register_31 (.D(In), .en(W_R29), .Q(R29), .clk(Clk), .clr(Rst));
  Register #(.width(32)) register_32 (.D(In), .en(W_R30), .Q(R30), .clk(Clk), .clr(Rst));
  Register #(.width(32)) register_33 (.D(In), .en(SP_EN), .Q(SP_Output), .clk(Clk), .clr(Rst));
  Multiplexer #(.select(5), .width(32)) multiplexer_1 (
    .in0({32{1'b0}}), .in1(R1), .in2(R2), .in3(R3), .in4(R4), .in5(R5), .in6(R6), .in7(R7), .in8(R8),
    .in9(R9), .in10(R10), .in11(R11), .in12(R12), .in13(R13), .in14(R14), .in15(R15), .in16(R16), .in17(R17),
    .in18(R18), .in19(R19), .in20(R20), .in21(R21), .in22(R22), .in23(R23), .in24(R24), .in25(R25),
    .in26(R26), .in27(R27), .in28(R28), .in29(R29), .in30(R30), .in31(SPOut), .out(A_out), .sel(Sa));  // open: en
  Multiplexer #(.select(5), .width(32)) multiplexer_2 (
    .in0({32{1'b0}}), .in1(R1), .in2(R2), .in3(R3), .in4(R4), .in5(R5), .in6(R6), .in7(R7), .in8(R8),
    .in9(R9), .in10(R10), .in11(R11), .in12(R12), .in13(R13), .in14(R14), .in15(R15), .in16(R16), .in17(R17),
    .in18(R18), .in19(R19), .in20(R20), .in21(R21), .in22(R22), .in23(R23), .in24(R24), .in25(R25),
    .in26(R26), .in27(R27), .in28(R28), .in29(R29), .in30(R30), .in31(SPOut), .out(B_out), .sel(Sb));  // open: en

  // Other names for the same wires on the sheet: Hi_In[31:0] = Hi; Hi_t[31:0] = Hi_2; Lo_In[31:0] = Lo;
  //   Lo_t[31:0] = Lo_2; SP_Out[31:0] = SP_Output

  // Notes on the sheet:
  //   Inputs
  //   Select register to write
  //   Lo Hi
  //   Registers R0-R31
  //   Output selector
  //   Output
endmodule

module ALU (
  input  [31:0] A,
  input  [31:0] B,
  input  [2:0] Op,
  output [31:0] Result,
  output Zero,
  output Negative,
  output [31:0] Lo,
  output [31:0] Hi
);

  wire comparator_1_lt, comparator_2_lt;
  wire [31:0] add, \and , div_Hi, div_Lo, divu_Hi, divu_Lo, mult_Hi, mult_Lo, mulu_Hi, mulu_Lo, \nor , \or ,
       slt, sltu, sub, \xor ;

  Adder #(.width(32)) adder_1 (.a(A), .b(B), .out(add));  // open: cin, cout
  Subtractor #(.width(32)) subtractor_1 (.a(A), .b(B), .out(sub));  // open: bin, bout
  assign \xor  = A ^ B;  // XOR_Gate xor_1, 32 bits wide
  assign \or  = A | B;  // OR_Gate or_1, 32 bits wide
  assign \nor  = ~\or ;  // NOT_Gate not_1, 32 bits wide
  assign \and  = A & B;  // AND_Gate and_1, 32 bits wide
  Multiplier #(.width(32)) multiplier_1 (.a(A), .b(B), .out(mulu_Lo), .cout(mulu_Hi));  // open: cin
  Signed_Multiplication signed_multiplication_1 (.A(A), .B(B), .Lo(mult_Lo), .Hi(mult_Hi));
  Comparator #(.width(32), .mode("unsigned")) comparator_1 (.a(A), .b(B), .lt(comparator_1_lt));  // open: gt, eq
  assign sltu = {{31{1'b0}}, comparator_1_lt};  // Bit_Extender bit_extender_1
  Comparator #(.width(32)) comparator_2 (.a(A), .b(B), .lt(comparator_2_lt));  // open: gt, eq
  assign slt = {{31{1'b0}}, comparator_2_lt};  // Bit_Extender bit_extender_2
  Divider #(.width(32)) divider_1 (.a(A), .b(B), .out(divu_Lo), .rem(divu_Hi));  // open: upper
  Signed_Division signed_division_1 (.A(A), .B(B), .Lo(div_Lo), .Hi(div_Hi));
  Multiplexer #(.select(3), .width(32), .enable("false")) multiplexer_1 (
    .in0(add), .in1(sub), .in2(\or ), .in3(\nor ), .in4(\xor ), .in5(\and ), .in6(slt), .in7(sltu),
    .out(Result), .sel(Op));
  Multiplexer #(.select(2), .width(32), .enable("false")) multiplexer_2 (
    .in0(mult_Lo), .in1(mulu_Lo), .in2(div_Lo), .in3(divu_Lo), .out(Lo), .sel(Op[1:0]));
  Multiplexer #(.select(2), .width(32), .enable("false")) multiplexer_3 (
    .in0(mult_Hi), .in1(mulu_Hi), .in2(div_Hi), .in3(divu_Hi), .out(Hi), .sel(Op[1:0]));
  Comparator #(.width(32)) comparator_3 (.a(Result), .b({32{1'b0}}), .eq(Zero), .lt(Negative));  // open: gt

  // Other names for the same wires on the sheet: Mul_Div[1:0] = Op[1:0]

  // Notes on the sheet:
  //   000=add
  //   001=sub
  //   010=or
  //   011=nor
  //   100=xor
  //   101=and
  //   110=slt
  //   111=sltu
  //   Los Op son los sigientes:
  //   Unsigned
  //   Signed
  //   00=mul
  //   01=mulu
  //   10=div
  //   11=divu
  //   Esto se puede hacer por la forma en que esta construido el RF
  //   Los Op de la division y la multiplicacion son:
endmodule

module Signed_Multiplication (
  input  [31:0] A,
  input  [31:0] B,
  output [31:0] Lo,
  output [31:0] Hi
);

  wire A_Sign, adder_1_cout, B_Sign, Result_Sign;
  wire [31:0] denier_1_x_2, denier_2_x_2, minus_Hi, minus_Lo, not_1_out, not_2_out, plus_Hi, plus_Lo;

  Denier denier_1 (.X(A), .Negative(A_Sign), .x_2(denier_1_x_2));
  Denier denier_2 (.X(B), .Negative(B_Sign), .x_2(denier_2_x_2));
  xor xor_1 (Result_Sign, A_Sign, B_Sign);
  Multiplier #(.width(32)) multiplier_1 (
    .a(denier_1_x_2), .b(denier_2_x_2), .out(plus_Lo), .cout(plus_Hi));  // open: cin
  assign not_1_out = ~plus_Lo;  // NOT_Gate not_1, 32 bits wide
  assign not_2_out = ~plus_Hi;  // NOT_Gate not_2, 32 bits wide
  Adder #(.width(32)) adder_1 (.a(not_1_out), .b(32'h1), .out(minus_Lo), .cout(adder_1_cout));  // open: cin
  Adder #(.width(32)) adder_2 (.a(not_2_out), .b({32{1'b0}}), .out(minus_Hi), .cin(adder_1_cout));  // open: cout
  Multiplexer #(.width(32), .enable("false")) multiplexer_1 (
    .in0(plus_Lo), .in1(minus_Lo), .out(Lo), .sel(Result_Sign));
  Multiplexer #(.width(32), .enable("false")) multiplexer_2 (
    .in0(plus_Hi), .in1(minus_Hi), .out(Hi), .sel(Result_Sign));
endmodule

module Signed_Division (
  input  [31:0] A,
  input  [31:0] B,
  output [31:0] Lo,
  output [31:0] Hi
);

  wire A_Sign, B_Sign, Quotient_Sign;
  wire [31:0] denier_1_x_2, denier_2_x_2, minus_Quotient, minus_Rest, plus_Quotient, plus_Rest;

  Denier denier_1 (.X(A), .Negative(A_Sign), .x_2(denier_1_x_2));
  Denier denier_2 (.X(B), .Negative(B_Sign), .x_2(denier_2_x_2));
  xor xor_1 (Quotient_Sign, A_Sign, B_Sign);
  Divider #(.width(32)) divider_1 (
    .a(denier_1_x_2), .b(denier_2_x_2), .out(plus_Quotient), .rem(plus_Rest));  // open: upper
  Negator #(.width(32)) negator_1 (.in(plus_Quotient), .out(minus_Quotient));
  Negator #(.width(32)) negator_2 (.in(plus_Rest), .out(minus_Rest));
  Multiplexer #(.width(32), .enable("false")) multiplexer_1 (
    .in0(plus_Quotient), .in1(minus_Quotient), .out(Lo), .sel(Quotient_Sign));
  Multiplexer #(.width(32), .enable("false")) multiplexer_2 (.in0(plus_Rest), .in1(minus_Rest), .out(Hi), .sel(A_Sign));
endmodule

module Denier (
  input  [31:0] X,
  output [31:0] x_2,
  output Negative
);

  wire [31:0] negator_1_out;

  Multiplexer #(.width(32), .enable("false")) multiplexer_1 (.in0(X), .in1(negator_1_out), .out(x_2), .sel(X[31]));
  Negator #(.width(32)) negator_1 (.in(X), .out(negator_1_out));

  assign Negative = X[31];
endmodule

module Instruction_Splitter (
  input  [31:0] Instruction,
  input  Clk,
  input  Reset,
  input  Instruction_Memory_R_W,
  output [5:0] OpCode,
  output [4:0] Rs,
  output [4:0] Rt,
  output [4:0] Rd,
  output [5:0] FuncCode,
  output [31:0] Signed_Constant,
  output [31:0] Unsigned_Constant,
  output [25:0] Jump_Target
);

  Register #(.width(32)) register_1 (
    .D(Instruction), .en(Instruction_Memory_R_W), .Q({OpCode, Jump_Target[25:6], FuncCode}), .clk(Clk),
    .clr(Reset));
  assign Signed_Constant = {{16{Jump_Target[15]}}, {Jump_Target[15:6], FuncCode}};  // Bit_Extender bit_extender_1
  assign Unsigned_Constant = {{16{1'b0}}, {Jump_Target[15:6], FuncCode}};  // Bit_Extender bit_extender_2

  assign Jump_Target[5:0] = FuncCode;
  assign Rd = Jump_Target[15:11];
  assign Rs = Jump_Target[25:21];
  assign Rt = Jump_Target[20:16];

  // Other names for the same wires on the sheet: Const[15:0] = {Jump_Target[15:6], FuncCode};
  //   Func_Code[5:0] = FuncCode; Target[25:0] = {Jump_Target[25:6], FuncCode}; Op_Code[5:0] = OpCode; Rst = Reset;
  //   W_R = Instruction_Memory_R_W

  // Notes on the sheet:
  //   Inputs
  //   Instruction
  //   Memory
  //   Split Instructions
  //   Outputs
endmodule

module Branch_Control (
  input  [31:0] PC,
  input  [25:0] Target,
  input  [31:0] Constant,
  input  [31:0] Register_Value,
  input  [1:0] Branch_Type_Selector,
  input  [2:0] Flag_Selector,
  input  Zero_Flag,
  input  Negative_Flag,
  output [31:0] PC_prime
);

  wire Flag, gtz, lez, ne;
  wire [31:0] Increment, offset_4, PC_4, PC_4_offset_4;

  and and_1 (gtz, ~Zero_Flag, ~Negative_Flag);  // AND_Gate
  Multiplexer #(.select(3)) multiplexer_1 (
    .in0(Zero_Flag), .in1(ne), .in2(lez), .in3(gtz), .in4(Negative_Flag), .out(Flag), .sel(Flag_Selector));  // open: in5, in6, in7, en
  not not_1 (ne, Zero_Flag);
  or or_1 (lez, Zero_Flag, Negative_Flag);
  Shifter #(.width(32)) shifter_1 (.in(Constant), .\dist (5'b00010), .out(offset_4));
  Adder #(.width(32)) adder_1 (.a(PC), .b(32'h4), .out(PC_4));  // open: cin, cout
  Adder #(.width(32)) adder_2 (.a(offset_4), .b(PC_4), .out(PC_4_offset_4));  // open: cin, cout
  Multiplexer #(.select(2), .width(32)) multiplexer_2 (
    .in0(PC_4), .in1(Register_Value), .in2({PC[31:28], Target, 2'b00}), .in3(Increment), .out(PC_prime),
    .sel(Branch_Type_Selector));  // open: en
  Multiplexer #(.width(32)) multiplexer_3 (.in0(PC_4), .in1(PC_4_offset_4), .out(Increment), .sel(Flag));  // open: en

  // Other names for the same wires on the sheet: BTS[1:0] = Branch_Type_Selector; Const[31:0] = Constant;
  //   eq = Zero_Flag; Z = Zero_Flag; FS[2:0] = Flag_Selector; Jump[31:2] = {PC[31:28], Target}; ltz = Negative_Flag;
  //   N = Negative_Flag; Reg[31:0] = Register_Value

  // Notes on the sheet:
  //   Inputs
  //   Branch Selector
  //   Branches
  //   PC Increment
  //   PC' Selector
  //   Increment Selector
  //   Output
endmodule

module Instruction_Decoder (
  input  [31:0] Instruction,
  input  Clk,
  input  Rst,
  input  R_W,
  output [31:0] Constant,
  output add,
  output mulu,
  output addi,
  output \nor ,
  output ori,
  output sltu,
  output mfhi,
  output sub,
  output div,
  output \and ,
  output \xor ,
  output xori,
  output slti,
  output mflo,
  output [4:0] RS,
  output mult,
  output divu,
  output \or ,
  output andi,
  output slt,
  output sltiu,
  output nop,
  output [4:0] RT,
  output [4:0] RD,
  output beq,
  output bne,
  output blez,
  output bgtz,
  output bltz,
  output j,
  output jr,
  output lw,
  output sw,
  output pop,
  output push,
  output halt,
  output tty,
  output rnd,
  output [25:0] Target,
  output kbd,
  output Type_I
);

  wire _000000, _111000, _111111, comparator_5_eq, comparator_6_eq, comparator_7_eq, comparator_8_eq,
       comparator_9_eq, comparator_10_eq, comparator_16_eq, comparator_17_eq, comparator_18_eq,
       comparator_19_eq, comparator_20_eq, comparator_21_eq, comparator_26_eq, comparator_27_eq,
       comparator_28_eq, comparator_29_eq, comparator_30_eq, comparator_35_eq, comparator_36_eq,
       comparator_37_eq, comparator_38_eq, comparator_39_eq, or_1_out;
  wire [5:0] FuncCode, OpCode;
  wire [31:0] SC, UC;

  Comparator #(.width(6), .mode("unsigned")) comparator_1 (.a(OpCode), .b({6{1'b0}}), .eq(_000000));  // open: gt, lt
  Comparator #(.width(6), .mode("unsigned")) comparator_2 (.a(OpCode), .b(6'b001000), .eq(addi));  // open: gt, lt
  Comparator #(.width(6), .mode("unsigned")) comparator_3 (.a(OpCode), .b(6'b000100), .eq(beq));  // open: gt, lt
  Comparator #(.width(6), .mode("unsigned")) comparator_4 (.a(OpCode), .b(6'b000111), .eq(bgtz));  // open: gt, lt
  Comparator #(.width(6), .mode("unsigned")) comparator_5 (
    .a(FuncCode), .b(6'b100000), .eq(comparator_5_eq));  // open: gt, lt
  Comparator #(.width(6), .mode("unsigned")) comparator_6 (
    .a(FuncCode), .b(6'b011001), .eq(comparator_6_eq));  // open: gt, lt
  Comparator #(.width(6), .mode("unsigned")) comparator_7 (
    .a(FuncCode), .b(6'b010000), .eq(comparator_7_eq));  // open: gt, lt
  Comparator #(.width(6), .mode("unsigned")) comparator_8 (
    .a(FuncCode), .b(6'b101010), .eq(comparator_8_eq));  // open: gt, lt
  Comparator #(.width(6), .mode("unsigned")) comparator_9 (
    .a(FuncCode), .b({6{1'b0}}), .eq(comparator_9_eq));  // open: gt, lt
  Comparator #(.width(6), .mode("unsigned")) comparator_10 (
    .a(FuncCode), .b(6'b000010), .eq(comparator_10_eq));  // open: gt, lt
  and and_1 (add, _000000, comparator_5_eq);
  and and_2 (mulu, _000000, comparator_6_eq);
  and and_3 (mfhi, _000000, comparator_7_eq);
  and and_4 (slt, _000000, comparator_8_eq);
  and and_5 (pop, _111000, comparator_9_eq);
  and and_6 (rnd, _111111, comparator_10_eq);
  Comparator #(.width(6), .mode("unsigned")) comparator_11 (.a(OpCode), .b({6{1'b1}}), .eq(_111111));  // open: gt, lt
  Comparator #(.width(6), .mode("unsigned")) comparator_12 (.a(OpCode), .b(6'b001100), .eq(andi));  // open: gt, lt
  Comparator #(.width(6), .mode("unsigned")) comparator_13 (.a(OpCode), .b(6'b000101), .eq(bne));  // open: gt, lt
  Comparator #(.width(6), .mode("unsigned")) comparator_14 (.a(OpCode), .b(6'b000001), .eq(bltz));  // open: gt, lt
  Comparator #(.width(6), .mode("unsigned")) comparator_15 (.a(OpCode), .b(6'b001110), .eq(xori));  // open: gt, lt
  and and_7 (sub, _000000, comparator_16_eq);
  Comparator #(.width(6), .mode("unsigned")) comparator_16 (
    .a(FuncCode), .b(6'b100010), .eq(comparator_16_eq));  // open: gt, lt
  and and_8 (div, _000000, comparator_17_eq);
  Comparator #(.width(6), .mode("unsigned")) comparator_17 (
    .a(FuncCode), .b(6'b011010), .eq(comparator_17_eq));  // open: gt, lt
  and and_9 (mflo, _000000, comparator_18_eq);
  Comparator #(.width(6), .mode("unsigned")) comparator_18 (
    .a(FuncCode), .b(6'b010010), .eq(comparator_18_eq));  // open: gt, lt
  and and_10 (\or , _000000, comparator_19_eq);
  Comparator #(.width(6), .mode("unsigned")) comparator_19 (
    .a(FuncCode), .b(6'b100101), .eq(comparator_19_eq));  // open: gt, lt
  and and_11 (push, _111000, comparator_20_eq);
  Comparator #(.width(6), .mode("unsigned")) comparator_20 (
    .a(FuncCode), .b(6'b000001), .eq(comparator_20_eq));  // open: gt, lt
  and and_12 (kbd, _111111, comparator_21_eq);
  Comparator #(.width(6), .mode("unsigned")) comparator_21 (
    .a(FuncCode), .b(6'b000100), .eq(comparator_21_eq));  // open: gt, lt
  Instruction_Splitter instruction_splitter_1 (
    .Instruction(Instruction), .Clk(Clk), .Reset(Rst), .Instruction_Memory_R_W(R_W), .OpCode(OpCode),
    .Rs(RS), .Rt(RT), .Rd(RD), .FuncCode(FuncCode), .Signed_Constant(SC), .Unsigned_Constant(UC),
    .Jump_Target(Target));
  Comparator #(.width(6), .mode("unsigned")) comparator_22 (.a(OpCode), .b(6'b001010), .eq(slti));  // open: gt, lt
  Comparator #(.width(6), .mode("unsigned")) comparator_23 (.a(OpCode), .b(6'b001011), .eq(sltiu));  // open: gt, lt
  Comparator #(.width(6), .mode("unsigned")) comparator_24 (.a(OpCode), .b(6'b000110), .eq(blez));  // open: gt, lt
  Comparator #(.width(6), .mode("unsigned")) comparator_25 (.a(OpCode), .b(6'b000010), .eq(j));  // open: gt, lt
  Comparator #(.width(6), .mode("unsigned")) comparator_26 (
    .a(FuncCode), .b(6'b011000), .eq(comparator_26_eq));  // open: gt, lt
  Comparator #(.width(6), .mode("unsigned")) comparator_27 (
    .a(FuncCode), .b(6'b011011), .eq(comparator_27_eq));  // open: gt, lt
  Comparator #(.width(6), .mode("unsigned")) comparator_28 (
    .a(FuncCode), .b({6{1'b0}}), .eq(comparator_28_eq));  // open: gt, lt
  Comparator #(.width(6), .mode("unsigned")) comparator_29 (
    .a(FuncCode), .b(6'b101011), .eq(comparator_29_eq));  // open: gt, lt
  Comparator #(.width(6), .mode("unsigned")) comparator_30 (
    .a(FuncCode), .b({6{1'b1}}), .eq(comparator_30_eq));  // open: gt, lt
  Multiplexer #(.width(32)) multiplexer_1 (.in0(SC), .in1(UC), .out(Constant), .sel(or_1_out));  // open: en
  or or_1 (or_1_out, andi, xori, ori);
  Comparator #(.width(6), .mode("unsigned")) comparator_31 (.a(OpCode), .b(6'b100011), .eq(lw));  // open: gt, lt
  Comparator #(.width(6), .mode("unsigned")) comparator_32 (.a(OpCode), .b(6'b101011), .eq(sw));  // open: gt, lt
  Comparator #(.width(6), .mode("unsigned")) comparator_33 (.a(OpCode), .b(6'b111000), .eq(_111000));  // open: gt, lt
  Comparator #(.width(6), .mode("unsigned")) comparator_34 (.a(OpCode), .b(6'b001101), .eq(ori));  // open: gt, lt
  and and_13 (mult, _000000, comparator_26_eq);
  and and_14 (divu, _000000, comparator_27_eq);
  and and_15 (nop, _000000, comparator_28_eq);
  and and_16 (sltu, _000000, comparator_29_eq);
  and and_17 (halt, _111111, comparator_30_eq);
  Comparator #(.width(6), .mode("unsigned")) comparator_35 (
    .a(FuncCode), .b(6'b100100), .eq(comparator_35_eq));  // open: gt, lt
  Comparator #(.width(6), .mode("unsigned")) comparator_36 (
    .a(FuncCode), .b(6'b101000), .eq(comparator_36_eq));  // open: gt, lt
  Comparator #(.width(6), .mode("unsigned")) comparator_37 (
    .a(FuncCode), .b(6'b100111), .eq(comparator_37_eq));  // open: gt, lt
  Comparator #(.width(6), .mode("unsigned")) comparator_38 (
    .a(FuncCode), .b(6'b001000), .eq(comparator_38_eq));  // open: gt, lt
  Comparator #(.width(6), .mode("unsigned")) comparator_39 (
    .a(FuncCode), .b(6'b000001), .eq(comparator_39_eq));  // open: gt, lt
  and and_18 (\and , _000000, comparator_35_eq);
  and and_19 (\xor , _000000, comparator_36_eq);
  and and_20 (\nor , _000000, comparator_37_eq);
  and and_21 (jr, _000000, comparator_38_eq);
  and and_22 (tty, _111111, comparator_39_eq);
  or or_2 (Type_I, bltz, addi, ori, slti, xori, slti, sltiu, beq, lw, andi, bne, sw, blez, bgtz);

  // Other names for the same wires on the sheet: C[31:0] = Constant; Inst[31:0] = Instruction

  // Notes on the sheet:
  //   OP-Code
  //   Func-Code
endmodule

module ALU_Selector (
  input  sub,
  input  \and ,
  input  slt,
  input  beq,
  input  add,
  input  bne,
  input  andi,
  input  slti,
  input  blez,
  input  addi,
  input  \or ,
  input  bgtz,
  input  mult,
  input  ori,
  input  bltz,
  input  mulu,
  input  \nor ,
  input  sltu,
  input  div,
  input  \xor ,
  input  sltiu,
  input  divu,
  input  xori,
  output [2:0] ALU_Code
);

  wire add_t, and_t, branch, or_2_out, or_8_out, or_9_out, or_t, slt_t, sltu_t, xor_t;

  or or_1 (add_t, add, addi);
  Multiplexer multiplexer_1 (.in0(1'b0), .in1(1'b1), .out(ALU_Code[0]), .sel(or_2_out));  // open: en
  or or_2 (or_2_out, and_t, mulu, divu, branch, sltu_t, sub, \nor );
  or or_3 (and_t, \and , andi);
  or or_4 (or_t, \or , ori);
  or or_5 (xor_t, \xor , xori);
  or or_6 (slt_t, slt, slti);
  or or_7 (sltu_t, sltu, sltiu);
  Multiplexer multiplexer_2 (.in0(1'b0), .in1(1'b1), .out(ALU_Code[1]), .sel(or_8_out));  // open: en
  or or_8 (or_8_out, slt_t, sltu_t, \nor , or_t, divu, div);
  or or_9 (or_9_out, slt_t, sltu_t, and_t, xor_t);
  or or_10 (branch, beq, bne, blez, bgtz, bltz);
  Multiplexer multiplexer_3 (.in0(1'b0), .in1(1'b1), .out(ALU_Code[2]), .sel(or_9_out));  // open: en

  // Other names for the same wires on the sheet: b0 = ALU_Code[0]; b1 = ALU_Code[1]; b2 = ALU_Code[2]
endmodule
